# Fritzing sketch reflektor (saved by Fritzing 0.6.5b)
breadboards: 1

parts:
  S1 = Pushbutton [package="[THT]"]
  J1 = Basic Servo
  J2 = Basic Servo
  J3 = Basic Servo
  Arduino1 = Arduino
  LED1 = LED - 5mm [color="Red (633nm)" package="5 mm [THT]"]
  LED2 = LED - 5mm [color="Red (633nm)" package="5 mm [THT]"]
  LED3 = LED - 5mm [color="Red (633nm)" package="5 mm [THT]"]
  R1 = Rotary Potentiometer (Large) [maximum_resistance=10kΩ package=THT]
  R2 = Resistor [tolerance=±5% resistance=220 package=THT]
  R3 = Resistor [tolerance=±5% resistance=220 package=THT]
  R4 = Resistor [tolerance=±5% resistance=220 package=THT]
  R5 = Resistor [tolerance=±5% resistance=220 package=THT]

nets:
  GND: S1.Pin_1, S1.Pin_2, J1.gnd, J2.gnd, J3.gnd, Arduino1.GND, LED2.cathode, LED3.cathode, R1.leg2
  N1: S1.Pin_3, S1.Pin_4, Arduino1.D3, R5.Pin_1
  VCC: J1.vcc, J2.vcc, J3.vcc, Arduino1.+5V, R1.leg1
  N2: J1.pulse, Arduino1.D9
  N3: J2.pulse, Arduino1.D10
  N4: J3.pulse, Arduino1.D11
  N5: Arduino1.D8, R2.Pin_0
  N6: Arduino1.D7, R3.Pin_0
  N7: Arduino1.D4, R4.Pin_0
  N8: Arduino1.A0, R1.wiper
  N9: LED1.anode, R4.Pin_1
  N10: LED2.anode, R2.Pin_1
  N11: LED3.anode, R3.Pin_1
